# Fritzing sketch Untitled Sketch (saved by Fritzing 0.7.10b)
breadboards: 1

parts:
  Arduino1 = Arduino
  R1 = Trimmer Potentiometer [maximum_resistance=10kΩ package=THT]
  J1 = Basic Servo

nets:
  GND: Arduino1.GND, R1.leg1, J1.gnd
  N1: Arduino1.D3, J1.pulse
  +5V: Arduino1.+5V, R1.leg2, J1.vcc
  N2: Arduino1.A5, R1.wiper
